# Fritzing sketch RC (saved by Fritzing 0.9.2b)
circuit board: 5.33097cm x 5.36429cm
breadboards: 1

parts:
  J1 = Basic Servo
  12V_power = Power plug
  Part1 = Arduino Uno (Rev3) - ICSP
  LDR = Photocell (LDR) [package=THT]
  part = Resistor [tolerance=±5% resistance=10k package=THT]

nets:
  GND: J1.gnd, 12V_power.GND, Part1.GND, part.Pin_1
  VCC: J1.vcc, Part1.5V, LDR.pin_0
  N1: J1.pulse, Part1.D3_PWM
  VCC_2: 12V_power.VCC, Part1.VIN
  N2: Part1.A0, LDR.pin_1, part.Pin_0
